# Fritzing sketch Btn (saved by Fritzing 0.9.3b)
breadboards: 1

parts:
  Part1 = ESPrDeveloper
  R4 = Resistor [tolerance=±5% resistance=10k package=THT]
  Part2 = BigBtn

nets:
  N1: Part1.3V3, R4.Pin_0
  N2: Part1.IO14, R4.Pin_1, Part2.2
  N3: Part1.GND#9, Part2.1

custom parts:
  ESPrDeveloper: ESPr developer is a one of the breakout board of the ESP8266
  BigBtn: Big Button
