# Fritzing sketch BtnLED (saved by Fritzing 0.9.3b)
breadboards: 1

parts:
  Part1 = ESPrDeveloper
  R4 = Resistor [tolerance=±5% resistance=10k package=THT]
  Part2 = BigBtn
  LED1 = LED - 5mm [color="Red (633nm)" package="5 mm [THT]"]
  R5 = Resistor [tolerance=±5% resistance=510 package=THT]  # not connected

nets:
  N1: Part1.IO14, Part2.2
  N2: Part1.IO13, LED1.anode
  N3: Part1.GND#9, R4.Pin_1, Part2.1

custom parts:
  ESPrDeveloper: ESPr developer is a one of the breakout board of the ESP8266
  BigBtn: Big Button
