# Fritzing sketch Button (saved by Fritzing 0.9.3b)
breadboards: 1

parts:
  Part1 = ESPrDeveloper
  R3 = Resistor [tolerance=±5% resistance=330 package=THT]
  LED1 = LED - 5mm [color="Red (633nm)" package="5 mm [THT]"]
  S1 = Momentary Switch [package=ksa_sealed_tac_switch]
  R4 = Resistor [tolerance=±5% resistance=10k package=THT]

nets:
  N1: Part1.IO13, LED1.anode
  N2: Part1.IO15, S1.4, R4.Pin_1
  N3: Part1.GND#9, R3.Pin_0, S1.2
  N4: R3.Pin_1, LED1.cathode

custom parts:
  ESPrDeveloper: ESPr developer is a one of the breakout board of the ESP8266
