# Fritzing sketch LED (saved by Fritzing 0.9.3b)
breadboards: 1

parts:
  Part1 = ESPrDeveloper
  LED1 = LED - 5mm [color="Red (633nm)" package="5 mm [THT]"]
  R4 = Resistor [tolerance=±5% resistance=510 package=THT]

nets:
  N1: Part1.IO12, LED1.anode
  N2: Part1.GND#9, R4.Pin_0
  N3: LED1.cathode, R4.Pin_1

custom parts:
  ESPrDeveloper: ESPr developer is a one of the breakout board of the ESP8266
