# Fritzing sketch MCP9808 (saved by Fritzing 0.9.3b)
breadboards: 1

parts:
  Part1 = ESPrDeveloper
  Part2 = MCP9808

nets:
  3V3: Part1.3V3, Part2.VDD
  N1: Part1.GND#9, Part2.GND
  N2: Part1.IO5, Part2.SCL
  N3: Part1.IO4, Part2.SDA

custom parts:
  ESPrDeveloper: ESPr developer is a one of the breakout board of the ESP8266
  MCP9808: temprerature sensor
