# Fritzing sketch Servo (saved by Fritzing 0.9.3b)
breadboards: 1

parts:
  Part1 = ESPrDeveloper
  J1 = Basic Servo
  VCC1 = Battery

nets:
  N1: Part1.IO13, J1.pulse
  N2: Part1.GND#19, J1.gnd, VCC1.-
  N3: J1.vcc, VCC1.+

custom parts:
  ESPrDeveloper: ESPr developer is a one of the breakout board of the ESP8266
