# Fritzing sketch StandAlone (saved by Fritzing 0.9.3b)
breadboards: 1

parts:
  Part1 = ESPrDeveloper
  LED1 = LED - 5mm [color="Red (633nm)" package="5 mm [THT]"]
  R5 = Resistor [tolerance=±5% resistance=510 package=THT]
  VCC1 = Battery

nets:
  N1: Part1.IO13, LED1.anode
  N2: Part1.GND#9, R5.Pin_0, VCC1.-
  N3: Part1.VIN, VCC1.+
  N4: LED1.cathode, R5.Pin_1

custom parts:
  ESPrDeveloper: ESPr developer is a one of the breakout board of the ESP8266
