# Fritzing sketch VCNL4010 (saved by Fritzing 0.9.3b)
breadboards: 1

parts:
  Part2 = VCNL4010
  Part1 = ESPrDeveloper

nets:
  VIN: Part2.VIN, Part1.3V3
  N1: Part2.GND, Part1.GND#9
  N2: Part2.SCL, Part1.IO5
  N3: Part2.SDA, Part1.IO4

custom parts:
  VCNL4010: distance and lux sensor
  ESPrDeveloper: ESPr developer is a one of the breakout board of the ESP8266
