# Fritzing sketch VCNL4010_LED (saved by Fritzing 0.9.3b)
breadboards: 1

parts:
  Part2 = VCNL4010
  Part1 = ESPrDeveloper
  R1 = Resistor [tolerance=±5% resistance=510 package=THT]
  LED1 = LED - 5mm [color="Red (633nm)" package="5 mm [THT]"]

nets:
  VIN: Part2.VIN, Part1.3V3
  N1: Part2.GND, Part1.GND#9, R1.Pin_0
  N2: Part2.SCL, Part1.IO5
  N3: Part2.SDA, Part1.IO4
  N4: Part1.IO13, LED1.anode
  N5: R1.Pin_1, LED1.cathode

custom parts:
  VCNL4010: distance and lux sensor
  ESPrDeveloper: ESPr developer is a one of the breakout board of the ESP8266
